# Fritzing sketch pull_up (saved by Fritzing 0.9.3b)

parts:
  Part1 = Arduino Uno (Rev3)
  R1 = Resistor [tolerance=±5% resistance=10k package=THT]

nets:
  N1: Part1.D7, R1.Pin_0
  N2: Part1.5V, R1.Pin_1
